// Digital circuit 3bit Adder.dig as structural Verilog
module _3bit_Adder (
  input  [2:0] I_2_0,
  output [2:0] O_2_0
);

  wire [0:0] not_1_out;
  wire [4:3] _5bitadder_1_s_4_0;

  not not_1 (not_1_out[0], 1'b0);
  _5bitAdder _5bitadder_1 (
    .A_4_0({2'b00, I_2_0}), .B_4_0({4'b0000, not_1_out[0]}), .Cin(1'b0), .S_4_0({_5bitadder_1_s_4_0, O_2_0}));  // open: Cout
endmodule
