// Digital circuit 3bit PC.dig as structural Verilog
module _3bit_PC (
  input  [2:0] I_2_0,
  input  CLK,
  output [2:0] O_2_0
);

  D_FF d_ff_1 (.D(I_2_0[0]), .C(CLK), .Q(O_2_0[0]));  // open: nQ
  D_FF d_ff_2 (.D(I_2_0[1]), .C(CLK), .Q(O_2_0[1]));  // open: nQ
  D_FF d_ff_3 (.D(I_2_0[2]), .C(CLK), .Q(O_2_0[2]));  // open: nQ
endmodule
