// Digital circuit 5bit ALU.dig as structural Verilog
module _5bit_ALU (
  input  [4:0] A_4_0,
  input  [4:0] B_4_0,
  input  [1:0] OP_1_0,
  output [4:0] R_4_0,
  output CF
);

  wire [4:0] ADD, AND, ROR;

  _5bitAdder _5bitadder_1 (.A_4_0(A_4_0), .B_4_0(B_4_0), .Cin(1'b0), .S_4_0(ADD), .Cout(CF));
  _5bitAnd _5bitand_1 (.A_4_0(A_4_0), .B_4_0(B_4_0), .O_4_0(AND));
  _5bitROR _5bitror_1 (.A_4_0(A_4_0), .Shift_2_0(B_4_0[2:0]), .O_4_0(ROR));
  Multiplexer #(.Selector_Bits(2), .Bits(5)) multiplexer_1 (
    .sel(OP_1_0), .in_0(ADD), .in_1(AND), .in_2(ROR), .in_3({5{1'b0}}), .out(R_4_0));

  // Other names for the same wires on the sheet: A[4:0] = A_4_0; B[4:0] = B_4_0; Shift[2:0] = B_4_0[2:0]
endmodule
