// Digital circuit 5bitAdder.dig as structural Verilog
module _5bitAdder (
  input  [4:0] A_4_0,
  input  [4:0] B_4_0,
  input  Cin,
  output Cout,
  output [4:0] S_4_0
);

  wire fa_2_cout, fa_3_cout, fa_4_cout, fa_5_cout;

  FA fa_1 (.Y(B_4_0[4]), .X(A_4_0[4]), .Cin(fa_2_cout), .S(S_4_0[4]), .Cout(Cout));
  FA fa_2 (.Y(B_4_0[3]), .X(A_4_0[3]), .Cin(fa_3_cout), .S(S_4_0[3]), .Cout(fa_2_cout));
  FA fa_3 (.Y(B_4_0[2]), .X(A_4_0[2]), .Cin(fa_4_cout), .S(S_4_0[2]), .Cout(fa_3_cout));
  FA fa_4 (.Y(B_4_0[1]), .X(A_4_0[1]), .Cin(fa_5_cout), .S(S_4_0[1]), .Cout(fa_4_cout));
  FA fa_5 (.Y(B_4_0[0]), .X(A_4_0[0]), .Cin(Cin), .S(S_4_0[0]), .Cout(fa_5_cout));
endmodule
