// Digital circuit 5bitAnd.dig as structural Verilog
module _5bitAnd (
  input  [4:0] A_4_0,
  input  [4:0] B_4_0,
  output [4:0] O_4_0
);

  and and_1 (O_4_0[4], A_4_0[4], B_4_0[4]);
  and and_2 (O_4_0[3], A_4_0[3], B_4_0[3]);
  and and_3 (O_4_0[2], A_4_0[2], B_4_0[2]);
  and and_4 (O_4_0[1], A_4_0[1], B_4_0[1]);
  and and_5 (O_4_0[0], A_4_0[0], B_4_0[0]);

  // Other names for the same wires on the sheet: A0 = A_4_0[0]; A1 = A_4_0[1]; A2 = A_4_0[2]; A3 = A_4_0[3];
  //   A4 = A_4_0[4]; B0 = B_4_0[0]; B1 = B_4_0[1]; B2 = B_4_0[2]; B3 = B_4_0[3]; B4 = B_4_0[4]; O0 = O_4_0[0];
  //   O1 = O_4_0[1]; O2 = O_4_0[2]; O3 = O_4_0[3]; O4 = O_4_0[4]

  // Notes on the sheet:
  //   A_4_0: default 17
  //   B_4_0: default 17
endmodule
