// Digital circuit 5bitRegister.dig as structural Verilog
module _5bitRegister (
  input  [4:0] Din_4_0,
  input  Sel,
  input  CLK,
  output [4:0] Dout_4_0
);

  _1bitRegister _1bitregister_1 (.Din(Din_4_0[4]), .Sel(Sel), .CLK(CLK), .Dout(Dout_4_0[4]));
  _1bitRegister _1bitregister_2 (.Din(Din_4_0[3]), .Sel(Sel), .CLK(CLK), .Dout(Dout_4_0[3]));
  _1bitRegister _1bitregister_3 (.Din(Din_4_0[2]), .Sel(Sel), .CLK(CLK), .Dout(Dout_4_0[2]));
  _1bitRegister _1bitregister_4 (.Din(Din_4_0[1]), .Sel(Sel), .CLK(CLK), .Dout(Dout_4_0[1]));
  _1bitRegister _1bitregister_5 (.Din(Din_4_0[0]), .Sel(Sel), .CLK(CLK), .Dout(Dout_4_0[0]));
endmodule
