// Digital circuit 7x15 SRAM.dig as structural Verilog
module _7x15_SRAM (
  input  [14:0] WD_14_0,
  input  WE,
  input  [2:0] WA_2_0,
  input  [2:0] RA1_2_0,
  input  [2:0] RA2_2_0,
  input  CLK,
  output [14:0] RD1_14_0,
  output [14:0] RD2_14_0
);

  wire decoder_3_out_0, decoder_3_out_1, decoder_3_out_2, decoder_3_out_3, decoder_3_out_4, decoder_3_out_5,
       decoder_3_out_6, R1_0, R1_1, R1_2, R1_3, R1_4, R1_5, R1_6, R2_0, R2_1, R2_2, R2_3, R2_4, R2_5, R2_6,
       W_0, W_1, W_2, W_3, W_4, W_5, W_6;
  wire [14:0] RD1_0, RD1_1, RD1_2, RD1_3, RD1_4, RD1_5, RD1_6, RD2_0, RD2_1, RD2_2, RD2_3, RD2_4, RD2_5,
       RD2_6;

  Decoder #(.Selector_Bits(3)) decoder_1 (
    .sel(RA1_2_0), .out_0(R1_0), .out_1(R1_1), .out_2(R1_2), .out_3(R1_3), .out_4(R1_4), .out_5(R1_5),
    .out_6(R1_6));  // open: out_7
  Decoder #(.Selector_Bits(3)) decoder_2 (
    .sel(RA2_2_0), .out_0(R2_0), .out_1(R2_1), .out_2(R2_2), .out_3(R2_3), .out_4(R2_4), .out_5(R2_5),
    .out_6(R2_6));  // open: out_7
  Decoder #(.Selector_Bits(3)) decoder_3 (
    .sel(WA_2_0), .out_0(decoder_3_out_0), .out_1(decoder_3_out_1), .out_2(decoder_3_out_2),
    .out_3(decoder_3_out_3), .out_4(decoder_3_out_4), .out_5(decoder_3_out_5), .out_6(decoder_3_out_6));  // open: out_7
  and and_1 (W_0, WE, decoder_3_out_0);
  and and_2 (W_1, decoder_3_out_1, WE);
  and and_3 (W_2, decoder_3_out_2, WE);
  and and_4 (W_3, decoder_3_out_3, WE);
  and and_5 (W_4, decoder_3_out_4, WE);
  and and_6 (W_5, decoder_3_out_5, WE);
  and and_7 (W_6, decoder_3_out_6, WE);
  _1x15_SRAM _1x15_sram_1 (
    .RS1(R1_0), .RS2(R2_0), .WS(W_0), .WD_14_0(WD_14_0), .CLK(CLK), .RD1_14_0(RD1_0), .RD2_14_0(RD2_0));
  _1x15_SRAM _1x15_sram_2 (
    .RS1(R1_1), .RS2(R2_1), .WS(W_1), .WD_14_0(WD_14_0), .CLK(CLK), .RD1_14_0(RD1_1), .RD2_14_0(RD2_1));
  _1x15_SRAM _1x15_sram_3 (
    .RS1(R1_2), .RS2(R2_2), .WS(W_2), .WD_14_0(WD_14_0), .CLK(CLK), .RD1_14_0(RD1_2), .RD2_14_0(RD2_2));
  _1x15_SRAM _1x15_sram_4 (
    .RS1(R1_3), .RS2(R2_3), .WS(W_3), .WD_14_0(WD_14_0), .CLK(CLK), .RD1_14_0(RD1_3), .RD2_14_0(RD2_3));
  _1x15_SRAM _1x15_sram_5 (
    .RS1(R1_4), .RS2(R2_4), .WS(W_4), .WD_14_0(WD_14_0), .CLK(CLK), .RD1_14_0(RD1_4), .RD2_14_0(RD2_4));
  _1x15_SRAM _1x15_sram_6 (
    .RS1(R1_5), .RS2(R2_5), .WS(W_5), .WD_14_0(WD_14_0), .CLK(CLK), .RD1_14_0(RD1_5), .RD2_14_0(RD2_5));
  _1x15_SRAM _1x15_sram_7 (
    .RS1(R1_6), .RS2(R2_6), .WS(W_6), .WD_14_0(WD_14_0), .CLK(CLK), .RD1_14_0(RD1_6), .RD2_14_0(RD2_6));
  assign RD1_14_0 = RD1_0 | RD1_1 | RD1_2 | RD1_3 | RD1_4 | RD1_5 | RD1_6;  // Or or_1, 15 bits wide
  assign RD2_14_0 = RD2_0 | RD2_1 | RD2_2 | RD2_3 | RD2_4 | RD2_5 | RD2_6;  // Or or_2, 15 bits wide

  // Other names for the same wires on the sheet: WD[14:0] = WD_14_0
endmodule
