// Digital circuit CPU.dig as structural Verilog
module CPU (
  input  [2:0] WA_2_0,
  input  [14:0] WD_14_0,
  input  WE,
  input  CLK,
  input  PC_EN,
  input  [2:0] RA2,
  input  SF,
  input  ZF,
  output [14:0] RD2,
  output [4:0] OUTPUT
);

  wire _5bit_alu_1_cf, CF, CPU_CLK, Imm_SEL, JMP_SEL, REG_EN, SF_t, ZF_t;
  wire [1:0] OP, OP_1_0, R1, R2, Type_of_Op;
  wire [2:0] _3bit_adder_1_o_2_0, multiplexer_1_out, undriven;
  wire [4:0] multiplexer_2_out, registerset_1_a_4_0, registerset_1_b_4_0;
  wire [6:0] Don_t_Care;

  Multiplexer #(.Bits(3)) multiplexer_1 (
    .sel(JMP_SEL), .in_0(_3bit_adder_1_o_2_0), .in_1(Don_t_Care[2:0]), .out(multiplexer_1_out));
  _3bit_Adder _3bit_adder_1 (.I_2_0(undriven), .O_2_0(_3bit_adder_1_o_2_0));
  _3bit_PC _3bit_pc_1 (.I_2_0(multiplexer_1_out), .CLK(CPU_CLK));  // open: O_2_0
  and and_1 (CPU_CLK, PC_EN, CLK);
  _7x15_SRAM _7x15_sram_1 (
    .RA1_2_0(undriven), .RA2_2_0(RA2), .WA_2_0(WA_2_0), .WD_14_0(WD_14_0), .WE(WE), .CLK(CLK),
    .RD1_14_0({Type_of_Op, OP, R1, R2, Don_t_Care}), .RD2_14_0(RD2));
  RegisterSet registerset_1 (
    .Wr_1_0(R1), .CLK(CPU_CLK), .REG_EN(REG_EN), .Wrd_4_0(OUTPUT), .Ra_1_0(R1), .Rb_1_0(R2),
    .A_4_0(registerset_1_a_4_0), .B_4_0(registerset_1_b_4_0));
  _5bit_ALU _5bit_alu_1 (
    .A_4_0(registerset_1_a_4_0), .B_4_0(multiplexer_2_out), .OP_1_0(OP), .R_4_0(OUTPUT), .CF(_5bit_alu_1_cf));
  FLAG_REG flag_reg_1 (.CF(_5bit_alu_1_cf), .ZF(ZF), .SF(SF), .CF_0(CF), .ZF_0(ZF_t), .SF_0(SF_t), .CLK(CPU_CLK));
  Multiplexer #(.Bits(5)) multiplexer_2 (
    .sel(Imm_SEL), .in_0(registerset_1_b_4_0), .in_1({R2, Don_t_Care[6:4]}), .out(multiplexer_2_out));
  Control_Unit control_unit_1 (
    .Opcode_3_0({Type_of_Op, OP}), .Imm_sel(Imm_SEL), .REG_EN(REG_EN), .OP_1_0(OP_1_0), .JPM_SEL(JMP_SEL),
    .CF(CF), .ZF(ZF_t), .SF(SF_t));

  // Other names for the same wires on the sheet: WA[2:0] = WA_2_0; WD[14:0] = WD_14_0

  // Notes on the sheet:
  //   WD_14_0: default 8464
  //   Type (2) + OP (2) + R1 (2) + R2 (2) + don't care (7)
  //   Type (2) + OP (2) + R1 (2) + (5) + don't care (4)
endmodule
