// Digital circuit Control Unit.dig as structural Verilog
module Control_Unit (
  input  [3:0] Opcode_3_0,
  input  CF,
  input  ZF,
  input  SF,
  output Imm_sel,
  output REG_EN,
  output [1:0] OP_1_0,
  output JPM_SEL
);

  wire and_2_out, and_3_out, and_4_out, and_6_out, or_1_out;

  and and_1 (Imm_sel, ~Opcode_3_0[3], Opcode_3_0[2]);  // And
  and and_2 (and_2_out, Opcode_3_0[3], ~Opcode_3_0[2]);  // And
  and and_3 (and_3_out, ~Opcode_3_0[1], ~Opcode_3_0[0]);  // And
  and and_4 (and_4_out, Opcode_3_0[3], ~Opcode_3_0[2]);  // And
  not not_1 (REG_EN, and_2_out);
  or or_1 (or_1_out, and_6_out, and_3_out);
  and and_5 (JPM_SEL, or_1_out, and_4_out);
  and and_6 (and_6_out, ~Opcode_3_0[1], Opcode_3_0[0], ZF, ~SF);  // And

  assign OP_1_0 = Opcode_3_0[1:0];

  // Other names for the same wires on the sheet: _2_3[1:0] = Opcode_3_0[3:2]

  // Notes on the sheet:
  //   Imm
  //   Jmp
  //   JMP
  //   JE
endmodule
