// Digital circuit FLAG REG.dig as structural Verilog
module FLAG_REG (
  input  CF,
  input  ZF,
  input  SF,
  input  CLK,
  output CF_0,
  output ZF_0,
  output SF_0
);

  wire not_1_out;

  not not_1 (not_1_out, 1'b0);
  _1bitRegister _1bitregister_1 (.Din(CF), .Sel(not_1_out), .CLK(CLK), .Dout(CF_0));
  _1bitRegister _1bitregister_2 (.Din(ZF), .Sel(not_1_out), .CLK(CLK), .Dout(ZF_0));
  _1bitRegister _1bitregister_3 (.Din(SF), .Sel(not_1_out), .CLK(CLK), .Dout(SF_0));
endmodule
