// Digital circuit RegisterSet.dig as structural Verilog
module RegisterSet (
  input  [1:0] Wr_1_0,
  input  [4:0] Wrd_4_0,
  input  CLK,
  input  [1:0] Ra_1_0,
  input  [1:0] Rb_1_0,
  input  REG_EN,
  output [4:0] A_4_0,
  output [4:0] B_4_0
);

  wire decoder_1_out_0, decoder_1_out_1, decoder_1_out_2, decoder_1_out_3, Reg0, Reg1, Reg2, Reg3;
  wire [4:0] R0, R1, R2, R3;

  Decoder #(.Selector_Bits(2)) decoder_1 (
    .sel(Wr_1_0), .out_0(decoder_1_out_0), .out_1(decoder_1_out_1), .out_2(decoder_1_out_2),
    .out_3(decoder_1_out_3));
  and and_1 (Reg0, REG_EN, decoder_1_out_0);
  and and_2 (Reg1, REG_EN, decoder_1_out_1);
  and and_3 (Reg2, REG_EN, decoder_1_out_2);
  and and_4 (Reg3, REG_EN, decoder_1_out_3);
  _5bitRegister _5bitregister_1 (.Din_4_0(Wrd_4_0), .Sel(Reg0), .CLK(CLK), .Dout_4_0(R0));
  _5bitRegister _5bitregister_2 (.Din_4_0(Wrd_4_0), .Sel(Reg1), .CLK(CLK), .Dout_4_0(R1));
  _5bitRegister _5bitregister_3 (.Din_4_0(Wrd_4_0), .Sel(Reg2), .CLK(CLK), .Dout_4_0(R2));
  _5bitRegister _5bitregister_4 (.Din_4_0(Wrd_4_0), .Sel(Reg3), .CLK(CLK), .Dout_4_0(R3));
  Multiplexer #(.Selector_Bits(2), .Bits(5)) multiplexer_1 (
    .sel(Ra_1_0), .in_0(R0), .in_1(R1), .in_2(R2), .in_3(R3), .out(A_4_0));
  Multiplexer #(.Selector_Bits(2), .Bits(5)) multiplexer_2 (
    .sel(Rb_1_0), .in_0(R0), .in_1(R1), .in_2(R2), .in_3(R3), .out(B_4_0));

  // Other names for the same wires on the sheet: Ra[1:0] = Ra_1_0; Rb[1:0] = Rb_1_0
endmodule
